# Fritzing sketch breathing_belt_arduino_connection (saved by Fritzing 0.7.0b)
breadboards: 1

parts:
  Arduino1 = Arduino
  U1 = mystery part, 3 pins [chip_label="trimmer 3386 resistor" spacing=300mil]
  U2 = mystery part, 3 pins [chip_label="trimmer 3386 resistor" spacing=300mil]
  R1 = Resistor [tolerance=±5% resistance=220 package=THT]

nets:
  N1: Arduino1.aref, U1.pin2, U2.pin1
  N2: Arduino1.3V3, U1.pin1
  N3: Arduino1.A0, R1.Pin_1
